# Fritzing sketch NodeMCU_DHT11 (saved by Fritzing 0.9.3b)

parts:
  U1 = NodeMCU V1.0
  DHT11 = DHT11 Humitidy and Temperature Sensor

nets:
  N1: U1.D2, DHT11.DATA
  N2: U1.GND, DHT11.NULL
  VIN: U1.Vin, DHT11.VDD

custom parts:
  NodeMCU V1.0: ESP8266 based NodeMCU
  DHT11 Humitidy and Temperature Sensor: DHT11 Humidity and Temperature Sensor
